# Fritzing sketch joulupurkkir (saved by Fritzing 0.7.10b)
breadboards: 1

parts:
  ATtiny = SOIC-14 [chip_label=IC package=SO]
  REG = Voltage Regulator - 5V [package="TO220 [THT]"]
  C1 = Electrolytic Capacitor [capacitance=100nF package="100 mil [THT, electrolytic]"]
  C2 = Electrolytic Capacitor [capacitance=33µF package="100 mil [THT, electrolytic]"]
  Q1 = NPN-Transistor [package="TO92 [THT]"]
  Q2 = NPN-Transistor [package="TO92 [THT]"]
  Q3 = NPN-Transistor [package="TO92 [THT]"]
  Q4 = NPN-Transistor [package="TO92 [THT]"]
  Q5 = NPN-Transistor [package="TO92 [THT]"]
  Q6 = NPN-Transistor [package="TO92 [THT]"]
  LEDS = double row female pin header, 14 pins [form="♀ (female)"]
  Q7 = NPN-Transistor [package="TO92 [THT]"]
  R7 = Resistor [tolerance=±5% resistance=1k package=THT]
  R6 = Resistor [tolerance=±5% resistance=1k package=THT]
  R5 = Resistor [tolerance=±5% resistance=1k package=THT]
  R4 = Resistor [tolerance=±5% resistance=1k package=THT]
  R3 = Resistor [tolerance=±5% resistance=1k package=THT]
  R2 = Resistor [tolerance=±5% resistance=1k package=THT]
  R1 = Resistor [tolerance=±5% resistance=1k package=THT]
  Power_plug = Power plug
  POWER = female pin header, 2 pins [form="♀ (female)"]
  ISP = Generic double row female header - 6 pins [form="♀ (female)" package=THT]
  POWER_2 = female pin header, 2 pins [form="♀ (female)"]
  switch = female pin header, 3 pins [form="♀ (female)"]

nets:
  N1: ATtiny.1, REG.output_voltage, C1.+, Q1.C, Q2.C, Q3.C, Q4.C, Q5.C, Q6.C, Q7.C, ISP.VTG
  GND: ATtiny.2, ATtiny.3, ATtiny.5, ATtiny.6, ATtiny.14, REG.GND, C1.-, C2.-, LEDS.pin8, LEDS.pin9, LEDS.pin10, LEDS.pin11, LEDS.pin12, LEDS.pin13, LEDS.pin14, ISP.GND, POWER_2.pin1
  N2: ATtiny.4, ISP.RESET
  N3: ATtiny.7, R7.Pin_0, ISP.MOSI
  N4: ATtiny.8, R6.Pin_0, ISP.MISO
  N5: ATtiny.9, R5.Pin_0, ISP.SCK
  N6: ATtiny.10, R4.Pin_0
  N7: ATtiny.11, R3.Pin_0
  N8: ATtiny.12, R2.Pin_0
  N9: ATtiny.13, R1.Pin_0
  N10: REG.input_voltage, C2.+, switch.pin2
  N11: Q1.E, LEDS.pin7
  N12: Q1.B, R1.Pin_1
  N13: Q2.E, LEDS.pin6
  N14: Q2.B, R2.Pin_1
  N15: Q3.E, LEDS.pin5
  N16: Q3.B, R3.Pin_1
  N17: Q4.E, LEDS.pin4
  N18: Q4.B, R4.Pin_1
  N19: Q5.E, LEDS.pin3
  N20: Q5.B, R5.Pin_1
  N21: Q6.E, LEDS.pin2
  N22: Q6.B, R6.Pin_1
  N23: LEDS.pin1, Q7.E
  N24: Q7.B, R7.Pin_1
  N25: Power_plug.VCC, POWER.pin1
  N26: Power_plug.GND, POWER.pin2
  N27: POWER_2.pin2, switch.pin3

custom parts:
  Generic double row female header - 6 pins: Generic double row female header
